// Logisim project scheme.circ as structural Verilog: 4 circuits, main circuit main
module main (
);

  wire cdm_8_mark5_1_p1, cdm_8_mark5_1_p2, cdm_8_mark5_1_p4, cdm_8_mark5_1_p5, cdm_8_mark5_1_p6,
       cdm_8_mark5_1_p7, cdm_8_mark5_1_p8, cdm_8_mark5_1_p9, cdm_8_mark5_1_p10, cdm_8_mark5_1_p11, clk,
       decoder_1_out0, decoder_1_out1, not_1_out;
  wire [7:0] cdm_8_mark5_1_p13, cdm_8_mark5_1_p14, controlled_buffer_1_out;
  wire [15:0] cdm_8_mark5_1_p12;

  video video_1 ();  // open: halted_3, halted_4, coordsIn, drawClk, draw, integrate, clrRow, clrFig, halted, halted_2
  tetris tetris_1 ();  // open: dir, rotate, getNew, cs, dataClk, dataIn, dataOut, figNext, fail
  Clock clock_1 (.out(clk));
  // Probe on cdm_8_mark5_1_p1
  // Probe on cdm_8_mark5_1_p2
  // Probe on cdm_8_mark5_1_p4
  // Probe on cdm_8_mark5_1_p8
  // Probe on cdm_8_mark5_1_p5
  // Probe on cdm_8_mark5_1_p6
  // Probe on cdm_8_mark5_1_p7
  Decoder #(.disabled(0)) decoder_1 (
    .out0(decoder_1_out0), .out1(decoder_1_out1), .sel(cdm_8_mark5_1_p9), .en(cdm_8_mark5_1_p10));
  // CdM_8_mark5 cdm_8_mark5_1: pin names not known; wires that end beside it: cdm_8_mark5_1_p1, cdm_8_mark5_1_p2, clk, cdm_8_mark5_1_p4, cdm_8_mark5_1_p5, cdm_8_mark5_1_p6, cdm_8_mark5_1_p7, cdm_8_mark5_1_p8, cdm_8_mark5_1_p9, cdm_8_mark5_1_p10, cdm_8_mark5_1_p11, cdm_8_mark5_1_p12, cdm_8_mark5_1_p13, cdm_8_mark5_1_p14, 1'b1
  not not_1 (not_1_out, cdm_8_mark5_1_p11);
  assign controlled_buffer_1_out = not_1_out ? cdm_8_mark5_1_p13 : 8'bz;  // Controlled_Buffer controlled_buffer_1
  assign cdm_8_mark5_1_p14 = cdm_8_mark5_1_p11 ? controlled_buffer_1_out : 8'bz;  // Controlled_Buffer controlled_buffer_2
  // Probe on controlled_buffer_1_out
  RAM ram_1 (
    .addr(cdm_8_mark5_1_p12[7:0]), .data(controlled_buffer_1_out), .sel(decoder_1_out1), .clk(clk),
    .ld(cdm_8_mark5_1_p11));  // open: clr
  ROM #(.addrWidth(16)) rom_1 (.addr(cdm_8_mark5_1_p12), .data(controlled_buffer_1_out), .sel(decoder_1_out0));

  // Notes on the sheet:
  //   ROM
endmodule

module tetris (
  input  [1:0] dir,
  input  rotate,
  input  getNew,
  input  cs,
  input  dataClk,
  input  [7:0] dataIn,
  output [7:0] dataOut,
  output [7:0] figNext,
  output fail
);

  wire and_1_out, and_2_out, and_3_out, and_4_out, and_5_out, and_6_out, and_7_out, and_8_out, and_9_out,
       and_10_out, and_11_out, and_12_out, comparator_1_eq, comparator_1_gt, comparator_2_eq,
       comparator_2_gt, comparator_3_eq, comparator_3_gt, comparator_4_eq, comparator_4_lt, dX, dY, or_1_out,
       or_3_out, or_4_out, or_5_out;
  wire [2:0] counter_1_q;
  wire [7:0] adder_1_out, adder_5_out, adder_6_out, adder_7_out, rom_1_data, shifter;
  wire [8:0] adder_2_out, adder_3_out, adder_4_out, controlled_buffer_4_out, figNum, offset, random_1_out;
  wire [8:8] divider_1_rem;

  and and_1 (and_1_out, dir[0], ~dir[1]);  // AND_Gate
  Shift_Register #(.width(8), .length(9), .parallel("false")) shift_register_1 (
    .shift(cs), .in(dataIn), .clk(dataClk));  // open: out, load, clr, d0, q0, d1, q1, d2, q2, d3, q3, d4, q4, d5, q5, d6, q6, d7, q7, d8, q8
  and and_2 (and_2_out, dX, and_1_out);
  and and_3 (and_3_out, and_1_out, dY);
  assign dataOut = and_3_out ? shifter : 8'bz;  // Controlled_Buffer controlled_buffer_1
  Multiplier #(.width(9)) multiplier_1 (.a(9'h8), .b(figNum), .out(offset));  // open: cin, cout
  Random #(.width(9)) random_1 (.clk(getNew), .out(random_1_out));  // open: next, clr
  Adder adder_1 (.a(8'h1), .b(shifter), .out(adder_1_out));  // open: cin, cout
  assign dataOut = and_2_out ? adder_1_out : 8'bz;  // Controlled_Buffer controlled_buffer_2
  Divider #(.width(9)) divider_1 (.a(random_1_out), .b(9'h7), .rem({divider_1_rem[8], figNext}));  // open: out, upper
  // Probe on {divider_1_rem[8], figNext}
  // Probe on figNum
  Register #(.width(9)) register_1 (.D({divider_1_rem[8], figNext}), .Q(figNum), .clk(getNew));  // open: en, clr
  Counter #(.width(3), .max('h7)) counter_1 (
    .count(cs), .Q(counter_1_q), .clk(and_4_out));  // open: load, D, carry, clr
  and and_4 (and_4_out, or_1_out, dataClk);
  or or_1 (or_1_out, rotate, getNew);
  Comparator #(.width(3)) comparator_1 (
    .a(3'b100), .b(counter_1_q), .gt(comparator_1_gt), .eq(comparator_1_eq), .lt(dX));
  and and_5 (and_5_out, ~dir[0], dir[1]);  // AND_Gate
  or or_2 (dY, comparator_1_gt, comparator_1_eq);
  Adder #(.width(9)) adder_2 (.a({{6{1'b0}}, counter_1_q}), .b(9'h28), .out(adder_2_out));  // open: cin, cout
  Adder #(.width(9)) adder_3 (.a({{6{1'b0}}, counter_1_q}), .b(offset), .out(adder_3_out));  // open: cin, cout
  and and_6 (and_6_out, dX, and_5_out);
  and and_7 (and_7_out, and_5_out, dY);
  assign dataOut = and_7_out ? shifter : 8'bz;  // Controlled_Buffer controlled_buffer_3
  assign controlled_buffer_4_out = rotate ? adder_4_out : 9'bz;  // Controlled_Buffer controlled_buffer_4
  Adder #(.width(9)) adder_4 (.a(adder_2_out), .b(offset), .out(adder_4_out));  // open: cin, cout
  assign controlled_buffer_4_out = getNew ? adder_3_out : 9'bz;  // Controlled_Buffer controlled_buffer_5
  Adder adder_5 (.a({8{1'b1}}), .b(shifter), .out(adder_5_out));  // open: cin, cout
  assign dataOut = and_6_out ? adder_5_out : 8'bz;  // Controlled_Buffer controlled_buffer_6
  Comparator comparator_2 (.a(dataOut), .b(8'h14), .gt(comparator_2_gt), .eq(comparator_2_eq));  // open: lt
  Comparator comparator_3 (.a(dataOut), .b(8'h10), .gt(comparator_3_gt), .eq(comparator_3_eq));  // open: lt
  Comparator comparator_4 (.a(dataOut), .b({8{1'b1}}), .eq(comparator_4_eq), .lt(comparator_4_lt));  // open: gt
  and and_8 (and_8_out, dY, or_3_out);
  or or_3 (or_3_out, comparator_2_gt, comparator_2_eq);
  and and_9 (and_9_out, dX, or_4_out);
  or or_4 (or_4_out, comparator_3_gt, comparator_3_eq);
  or or_5 (or_5_out, comparator_4_eq, comparator_4_lt);
  Adder adder_6 (.a(rom_1_data), .b(shifter), .out(adder_6_out));  // open: cin, cout
  ROM #(.addrWidth(9)) rom_1 (.addr(controlled_buffer_4_out), .data(rom_1_data));  // open: sel
  and and_10 (and_10_out, dY, and_11_out);
  and and_11 (and_11_out, dir[0], dir[1]);
  and and_12 (and_12_out, and_11_out, dX);
  or or_6 (fail, and_8_out, and_9_out, or_5_out);
  assign dataOut = getNew ? rom_1_data : 8'bz;  // Controlled_Buffer controlled_buffer_7
  assign dataOut = rotate ? adder_6_out : 8'bz;  // Controlled_Buffer controlled_buffer_8
  Adder adder_7 (.a({8{1'b1}}), .b(shifter), .out(adder_7_out));  // open: cin, cout
  assign dataOut = and_12_out ? shifter : 8'bz;  // Controlled_Buffer controlled_buffer_9
  assign dataOut = and_10_out ? adder_7_out : 8'bz;  // Controlled_Buffer controlled_buffer_10

  // Other names for the same wires on the sheet: figNextNum[7:0] = figNext; out[7:0] = dataOut

  // Notes on the sheet:
  //   MOVE RIGHT
  //   MOVE LEFT
  //   MOVE DOWN
endmodule

module video (
  input  [7:0] halted,
  input  [31:0] halted_2,
  input  halted_3,
  input  halted_4,
  input  [7:0] coordsIn,
  input  drawClk,
  input  draw,
  input  integrate,
  input  clrRow,
  input  clrFig
);

  wire and_1_out, fieldSt0, fieldSt1, fieldSt2, fieldSt3, not_1_out, or_1_out, videoram_2_clr,
       videoram_2_csout, videoram_3_clr, videoram_3_csout, videoram_4_clr, videoram_4_csout;
  wire [2:0] counter_1_q, row;
  wire [7:0] adder_1_out, divider_1_out, shifter, videoram_2_idout, videoram_2_rowo, videoram_3_idout,
       videoram_3_rowo, videoram_4_idout, videoram_4_rowo;
  wire [7:3] divider_1_rem;
  wire [31:0] data, shifter_1_out, shifter_2_out, videoram_2_dataout, videoram_2_halted, videoram_2_halted_2,
       videoram_2_halted_3, videoram_2_halted_4, videoram_2_halted_5, videoram_2_halted_6,
       videoram_2_halted_7, videoram_2_halted_8, videoram_2_lastout, videoram_3_dataout, videoram_3_halted,
       videoram_3_halted_2, videoram_3_halted_3, videoram_3_halted_4, videoram_3_halted_5,
       videoram_3_halted_6, videoram_3_halted_7, videoram_3_halted_8, videoram_3_lastout, videoram_4_dataout,
       videoram_4_halted, videoram_4_halted_2, videoram_4_halted_3, videoram_4_halted_4, videoram_4_halted_5,
       videoram_4_halted_6, videoram_4_halted_7, videoram_4_halted_8, videoram_4_lastout, videoram_5_halted,
       videoram_5_halted_2, videoram_5_halted_3, videoram_5_halted_4, videoram_5_halted_5,
       videoram_5_halted_6, videoram_5_halted_7, videoram_5_halted_8;

  not not_1 (not_1_out, clrRow);
  Shift_Register #(.width(8), .parallel("false")) shift_register_1 (
    .shift(not_1_out), .in(coordsIn), .clk(drawClk));  // open: out, load, clr, d0, q0, d1, q1, d2, q2, d3, q3, d4, q4, d5, q5, d6, q6, d7, q7
  Adder adder_1 (.a(coordsIn), .b(8'hc), .out(adder_1_out));  // open: cin, cout
  Counter #(.width(3), .max('h7)) counter_1 (
    .count(or_1_out), .Q(counter_1_q), .clk(drawClk));  // open: load, D, carry, clr
  or or_1 (or_1_out, draw, integrate);
  Shifter #(.width(32)) shifter_1 (.in({32{1'b1}}), .\dist (adder_1_out[4:0]), .out(shifter_1_out));
  Shifter #(.width(32), .shift("lr")) shifter_2 (.in(32'h80000000), .\dist (shifter[4:0]), .out(shifter_2_out));
  // Probe on shifter_1_out
  Register #(.width(32)) register_1 (.D(shifter_2_out), .en(and_1_out), .Q(data), .clk(drawClk));  // open: clr
  and and_1 (and_1_out, ~counter_1_q[0], or_1_out);  // AND_Gate
  Divider divider_1 (.a(shifter), .b(8'h4), .out(divider_1_out), .rem({divider_1_rem, row}));  // open: upper
  videoRam videoram_1 ();  // open: csOUT, CS, rowO, halted, row, data, halted_2, clrRow, clr, halted_3, idIN, halted_4, dataOut, halted_5, idOUT, halted_6, lastIn, halted_7, halted_8, lastOut
  Decoder #(.select(2)) decoder_1 (
    .out0(fieldSt0), .out1(fieldSt1), .out2(fieldSt2), .out3(fieldSt3), .sel(divider_1_out[1:0]), .en(draw));
  videoRam videoram_2 (
    .csOUT(videoram_2_csout), .CS(halted_4), .rowO(videoram_2_rowo), .halted(videoram_2_halted),
    .row(halted), .data(halted_2), .halted_2(videoram_2_halted_2), .clrRow(halted_3), .clr(videoram_2_clr),
    .halted_3(videoram_2_halted_3), .idIN({8{1'b0}}), .halted_4(videoram_2_halted_4),
    .dataOut(videoram_2_dataout), .halted_5(videoram_2_halted_5), .idOUT(videoram_2_idout),
    .halted_6(videoram_2_halted_6), .lastIn({32{1'b0}}), .halted_7(videoram_2_halted_7),
    .halted_8(videoram_2_halted_8), .lastOut(videoram_2_lastout));
  videoRam videoram_3 (
    .csOUT(videoram_3_csout), .CS(videoram_2_csout), .rowO(videoram_3_rowo), .halted(videoram_3_halted),
    .row(videoram_2_rowo), .data(videoram_2_dataout), .halted_2(videoram_3_halted_2),
    .clrRow(videoram_2_clr), .clr(videoram_3_clr), .halted_3(videoram_3_halted_3), .idIN(videoram_2_idout),
    .halted_4(videoram_3_halted_4), .dataOut(videoram_3_dataout), .halted_5(videoram_3_halted_5),
    .idOUT(videoram_3_idout), .halted_6(videoram_3_halted_6), .lastIn(videoram_2_lastout),
    .halted_7(videoram_3_halted_7), .halted_8(videoram_3_halted_8), .lastOut(videoram_3_lastout));
  videoRam videoram_4 (
    .csOUT(videoram_4_csout), .CS(videoram_3_csout), .rowO(videoram_4_rowo), .halted(videoram_4_halted),
    .row(videoram_3_rowo), .data(videoram_3_dataout), .halted_2(videoram_4_halted_2),
    .clrRow(videoram_3_clr), .clr(videoram_4_clr), .halted_3(videoram_4_halted_3), .idIN(videoram_3_idout),
    .halted_4(videoram_4_halted_4), .dataOut(videoram_4_dataout), .halted_5(videoram_4_halted_5),
    .idOUT(videoram_4_idout), .halted_6(videoram_4_halted_6), .lastIn(videoram_3_lastout),
    .halted_7(videoram_4_halted_7), .halted_8(videoram_4_halted_8), .lastOut(videoram_4_lastout));
  videoRam videoram_5 (
    .CS(videoram_4_csout), .halted(videoram_5_halted), .row(videoram_4_rowo), .data(videoram_4_dataout),
    .halted_2(videoram_5_halted_2), .clrRow(videoram_4_clr), .halted_3(videoram_5_halted_3),
    .idIN(videoram_4_idout), .halted_4(videoram_5_halted_4), .halted_5(videoram_5_halted_5),
    .halted_6(videoram_5_halted_6), .lastIn(videoram_4_lastout), .halted_7(videoram_5_halted_7),
    .halted_8(videoram_5_halted_8));  // open: csOUT, rowO, clr, dataOut, idOUT, lastOut
  // _32x32_4_bit_LCD 32x32_4_bit_lcd_1: pin names not known; wires that end beside it: videoram_2_halted_2, videoram_2_halted_3, videoram_2_halted_4, videoram_2_halted_5, videoram_2_halted_6, videoram_2_halted_7, videoram_2_halted_8, videoram_3_halted, videoram_3_halted_2, videoram_3_halted_3, videoram_3_halted_4, videoram_3_halted_5, videoram_3_halted_6, videoram_3_halted_7, videoram_3_halted_8, videoram_4_halted, videoram_4_halted_2, videoram_4_halted_3, videoram_4_halted_4, videoram_4_halted_5, videoram_4_halted_6, videoram_4_halted_7, videoram_4_halted_8, videoram_5_halted, videoram_5_halted_2, videoram_5_halted_3, videoram_5_halted_4, videoram_5_halted_5, videoram_5_halted_6, videoram_5_halted_7, videoram_5_halted_8, videoram_2_halted

  // Other names for the same wires on the sheet: dataClk = drawClk; input[7:0] = coordsIn; integr = integrate
endmodule

module videoRam (
  input  CS,
  input  [7:0] row,
  input  [31:0] data,
  input  clrRow,
  input  [7:0] idIN,
  input  [31:0] lastIn,
  output csOUT,
  output [7:0] rowO,
  output [31:0] halted,
  output [31:0] halted_2,
  output clr,
  output [31:0] halted_3,
  output [31:0] halted_4,
  output [31:0] dataOut,
  output [31:0] halted_5,
  output [7:0] idOUT,
  output [31:0] halted_6,
  output [31:0] halted_7,
  output [31:0] halted_8,
  output [31:0] lastOut
);

  wire and_1_out, comparator_1_eq, decoder_1_out0, decoder_1_out1, decoder_1_out2, decoder_1_out3,
       decoder_1_out4, decoder_1_out5, decoder_1_out6, decoder_1_out7, not_2_out, not_3_out, not_4_out,
       not_5_out, not_6_out, not_7_out, not_8_out, not_9_out;
  wire [7:0] divider_1_out, divider_1_rem, not_1_out, shifter_1_out;
  wire [31:0] controlled_buffer_9_out, controlled_buffer_11_out, controlled_buffer_13_out,
       controlled_buffer_15_out, controlled_buffer_17_out, controlled_buffer_19_out,
       controlled_buffer_21_out, controlled_buffer_23_out, or_1_out, or_2_out, or_3_out, or_4_out, or_5_out,
       or_6_out, or_7_out, or_8_out;

  Adder adder_1 (.a(8'h1), .b(idIN), .out(idOUT));  // open: cin, cout
  and and_1 (and_1_out, ~clrRow, comparator_1_eq);  // AND_Gate
  Comparator comparator_1 (.a(idIN), .b(divider_1_out), .eq(comparator_1_eq));  // open: gt, lt
  Divider divider_1 (.a(row), .b(8'h8), .out(divider_1_out), .rem(divider_1_rem));  // open: upper
  Decoder #(.select(3)) decoder_1 (
    .out0(decoder_1_out0), .out1(decoder_1_out1), .out2(decoder_1_out2), .out3(decoder_1_out3),
    .out4(decoder_1_out4), .out5(decoder_1_out5), .out6(decoder_1_out6), .out7(decoder_1_out7),
    .sel(divider_1_rem[2:0]), .en(and_1_out));
  // Probe on not_1_out
  Shifter shifter_1 (.in({8{1'b1}}), .\dist (divider_1_rem[2:0]), .out(shifter_1_out));
  assign not_1_out = ~shifter_1_out;  // NOT_Gate not_1, 8 bits wide
  Pull_Resistor pull_resistor_1 (.node(decoder_1_out0));
  Pull_Resistor pull_resistor_2 (.node(decoder_1_out1));
  Pull_Resistor pull_resistor_3 (.node(decoder_1_out2));
  Pull_Resistor pull_resistor_4 (.node(decoder_1_out3));
  Pull_Resistor pull_resistor_5 (.node(decoder_1_out4));
  Pull_Resistor pull_resistor_6 (.node(decoder_1_out5));
  Pull_Resistor pull_resistor_7 (.node(decoder_1_out6));
  Pull_Resistor pull_resistor_8 (.node(decoder_1_out7));
  assign decoder_1_out0 = clrRow ? not_1_out[0] : 1'bz;  // Controlled_Buffer controlled_buffer_1
  assign decoder_1_out1 = clrRow ? not_1_out[1] : 1'bz;  // Controlled_Buffer controlled_buffer_2
  assign decoder_1_out2 = clrRow ? not_1_out[2] : 1'bz;  // Controlled_Buffer controlled_buffer_3
  assign decoder_1_out3 = clrRow ? not_1_out[3] : 1'bz;  // Controlled_Buffer controlled_buffer_4
  assign decoder_1_out4 = clrRow ? not_1_out[4] : 1'bz;  // Controlled_Buffer controlled_buffer_5
  assign decoder_1_out5 = clrRow ? not_1_out[5] : 1'bz;  // Controlled_Buffer controlled_buffer_6
  assign decoder_1_out6 = clrRow ? not_1_out[6] : 1'bz;  // Controlled_Buffer controlled_buffer_7
  assign decoder_1_out7 = clrRow ? not_1_out[7] : 1'bz;  // Controlled_Buffer controlled_buffer_8
  assign or_1_out = data | halted;  // OR_Gate or_1, 32 bits wide
  assign or_2_out = data | halted_2;  // OR_Gate or_2, 32 bits wide
  assign or_3_out = data | halted_3;  // OR_Gate or_3, 32 bits wide
  assign or_4_out = data | halted_4;  // OR_Gate or_4, 32 bits wide
  assign or_5_out = data | halted_5;  // OR_Gate or_5, 32 bits wide
  assign or_6_out = data | halted_6;  // OR_Gate or_6, 32 bits wide
  assign or_7_out = data | halted_7;  // OR_Gate or_7, 32 bits wide
  assign or_8_out = data | halted_8;  // OR_Gate or_8, 32 bits wide
  assign controlled_buffer_9_out = clrRow ? lastIn : 32'bz;  // Controlled_Buffer controlled_buffer_9
  not not_2 (not_2_out, clrRow);
  assign controlled_buffer_9_out = not_2_out ? or_1_out : 32'bz;  // Controlled_Buffer controlled_buffer_10
  Register #(.width(32)) register_1 (
    .D(controlled_buffer_9_out), .en(decoder_1_out0), .Q(halted), .clk(CS));  // open: clr
  assign controlled_buffer_11_out = clrRow ? halted : 32'bz;  // Controlled_Buffer controlled_buffer_11
  not not_3 (not_3_out, clrRow);
  assign controlled_buffer_11_out = not_3_out ? or_2_out : 32'bz;  // Controlled_Buffer controlled_buffer_12
  Register #(.width(32)) register_2 (
    .D(controlled_buffer_11_out), .en(decoder_1_out1), .Q(halted_2), .clk(CS));  // open: clr
  assign controlled_buffer_13_out = clrRow ? halted_2 : 32'bz;  // Controlled_Buffer controlled_buffer_13
  not not_4 (not_4_out, clrRow);
  assign controlled_buffer_13_out = not_4_out ? or_3_out : 32'bz;  // Controlled_Buffer controlled_buffer_14
  Register #(.width(32)) register_3 (
    .D(controlled_buffer_13_out), .en(decoder_1_out2), .Q(halted_3), .clk(CS));  // open: clr
  assign controlled_buffer_15_out = clrRow ? halted_3 : 32'bz;  // Controlled_Buffer controlled_buffer_15
  not not_5 (not_5_out, clrRow);
  assign controlled_buffer_15_out = not_5_out ? or_4_out : 32'bz;  // Controlled_Buffer controlled_buffer_16
  Register #(.width(32)) register_4 (
    .D(controlled_buffer_15_out), .en(decoder_1_out3), .Q(halted_4), .clk(CS));  // open: clr
  assign controlled_buffer_17_out = clrRow ? halted_4 : 32'bz;  // Controlled_Buffer controlled_buffer_17
  not not_6 (not_6_out, clrRow);
  assign controlled_buffer_17_out = not_6_out ? or_5_out : 32'bz;  // Controlled_Buffer controlled_buffer_18
  Register #(.width(32)) register_5 (
    .D(controlled_buffer_17_out), .en(decoder_1_out4), .Q(halted_5), .clk(CS));  // open: clr
  assign controlled_buffer_19_out = clrRow ? halted_5 : 32'bz;  // Controlled_Buffer controlled_buffer_19
  not not_7 (not_7_out, clrRow);
  assign controlled_buffer_19_out = not_7_out ? or_6_out : 32'bz;  // Controlled_Buffer controlled_buffer_20
  Register #(.width(32)) register_6 (
    .D(controlled_buffer_19_out), .en(decoder_1_out5), .Q(halted_6), .clk(CS));  // open: clr
  assign controlled_buffer_21_out = clrRow ? halted_6 : 32'bz;  // Controlled_Buffer controlled_buffer_21
  not not_8 (not_8_out, clrRow);
  assign controlled_buffer_21_out = not_8_out ? or_7_out : 32'bz;  // Controlled_Buffer controlled_buffer_22
  Register #(.width(32)) register_7 (
    .D(controlled_buffer_21_out), .en(decoder_1_out6), .Q(halted_7), .clk(CS));  // open: clr
  assign controlled_buffer_23_out = clrRow ? halted_7 : 32'bz;  // Controlled_Buffer controlled_buffer_23
  not not_9 (not_9_out, clrRow);
  assign controlled_buffer_23_out = not_9_out ? or_8_out : 32'bz;  // Controlled_Buffer controlled_buffer_24
  Register #(.width(32)) register_8 (
    .D(controlled_buffer_23_out), .en(decoder_1_out7), .Q(halted_8), .clk(CS));  // open: clr

  assign clr = clrRow;
  assign csOUT = CS;
  assign dataOut = data;
  assign lastOut = halted_8;
  assign rowO = row;

  // Other names for the same wires on the sheet: id[7:0] = idIN
endmodule
